# Fritzing sketch 04 (saved by Fritzing 0.9.3b)
breadboards: 1

parts:
  Raspberry_Pi_1 = Raspberry Pi 3 [part_number=RPI-3-V1.2]
  PIR1 = PIR sensor
  LED1 = smd LED [color="Red (633nm)" package="1206 [SMD]"]
  R1 = Resistor [tolerance=±5% resistance=330 package="0603 [SMD]"]

nets:
  N1: Raspberry_Pi_1.GIPO4, PIR1.SIG
  GND: Raspberry_Pi_1.GND, PIR1.GND, R1.Pin_0
  N2: Raspberry_Pi_1.GIPO10, LED1.anode
  5V: Raspberry_Pi_1.5V, PIR1.VDD
  N3: LED1.cathode, R1.Pin_1
